# Fritzing sketch Breadboard_Layout (saved by Fritzing 1.0.2b)
breadboards: 1

parts:
  Part1 = Adafruit Si5351A Clock Generator [part_number="Adafruit #2045"]
  Part2 = Adafruit Pro Trinket 3.3V 12MHz [part_number="Adafruit #2010"]
  BATT1 = 4xAA Switchable Battery Pack w/Bare Wire
  S1 = Pushbutton [package="[THT]"]
  R1 = Resistor [tolerance=±5% power=0.25W resistance=100k package=THT]
  R2 = Resistor [tolerance=±5% power=0.25W resistance=100k package=THT]
  Q1 = NPN-Transistor [package="TO92 [THT]"]
  R3 = TRIMPOT [maximum_resistance=10kΩ knob_status=50% power=0.5W package=3386u]
  IC1 = 74HC08 Logic AND Gate [part_number=74HC08 package="DIP (Dual Inline) [THT]"]
  L1 = Inductor [package="400 mil [THT]"]  # not connected
  Part3 = Variable Capacitor [capacitance=100nF max_capacitance=10pF min_capacitance=2pF voltage=35V]
  LED2 = smd LED [color="Red (633nm)" package="0603 [SMD]"]
  LED5 = smd LED [color="Green (555nm)" package="0603 [SMD]"]
  R8 = Resistor [tolerance=±5% power=0.25W resistance=150 package=THT]
  R9 = Resistor [tolerance=±5% power=0.25W resistance=68 package=THT]
  R10 = Resistor [tolerance=±5% power=0.25W resistance=68 package=THT]
  R11 = Resistor [tolerance=±5% power=0.25W resistance=68 package=THT]
  R12 = Resistor [tolerance=±5% power=0.25W resistance=68 package=THT]
  R13 = Resistor [tolerance=±5% power=0.25W resistance=100k package=THT]
  LED6 = smd LED [color="Red (633nm)" package="0603 [SMD]"]
  LED7 = smd LED [color="Red (633nm)" package="0603 [SMD]"]
  LED8 = smd LED [color="Red (633nm)" package="0603 [SMD]"]
  L2 = Inductor [package="400 mil [THT]"]
  L3 = Inductor [package="400 mil [THT]"]  # not connected
  L4 = Inductor [package="400 mil [THT]"]  # not connected
  L5 = Inductor [package="400 mil [THT]"]
  S2 = SPST Switch [package=switch-spdt]
  C2 = Ceramic Capacitor [capacitance=10pF voltage=35V package="100 mil [THT, multilayer]"]

nets:
  VIN: Part1.VIN, Part2.+3V3, S1.Pin_3, S1.Pin_4, IC1.VCC, Part3.1, L5.pin_0, C2.1
  GND: Part1.GND, Part2.GND, BATT1.NEG, R2.Pin_0, Q1.C, IC1.GND, R8.Pin_0, R9.Pin_1, R10.Pin_1, R11.Pin_1, R12.Pin_1, R13.Pin_0
  N1: Part1.SDA, Part2.A4
  N2: Part1.CLK0, IC1.1A
  N3: Part2.VBAT, R1.Pin_0, S2.P
  N4: Part2.D8, S1.Pin_1, S1.Pin_2, R13.Pin_1
  N5: Part2.D6, LED8.anode
  N6: Part2.D5, LED7.anode
  N7: Part2.D4, LED6.anode
  N8: Part2.D3, LED2.anode
  N9: Part2.D12, IC1.1B
  N10: Part2.D13, LED5.anode
  N11: BATT1.POS, S2.O
  N12: Q1.E, Part3.0, L2.pin_1, C2.0
  N13: Q1.B, R3.WIPER
  N14: R3.CW, IC1.1Y
  N15: LED2.cathode, R9.Pin_0
  N16: LED5.cathode, R8.Pin_1
  N17: R10.Pin_0, LED6.cathode
  N18: R11.Pin_0, LED7.cathode
  N19: R12.Pin_0, LED8.cathode

custom parts:
  Adafruit Si5351A Clock Generator: Never hunt around for another crystal again, with the Si5351A clock generator breakout from Adafruit! This chip has a precision 25MHz crystal reference and internal PLL and dividers so it can generate just about any frequency, from <8KHz up to 150+ MHz. The Si5351A clock generator is an I2C controller clock generator. It uses the onboard precision clock to drive multiple PLL's and clock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
  Adafruit Pro Trinket 3.3V 12MHz: rinket's got a big sister in town - the Pro Trinket 3V! Pro Trinket combines everything you love about Trinket with the familiarity of the core Arduino chip, the ATmega328. It's like an Arduino Pro Mini with more pins and USB tossed in. Trinket's a year old now, and while its been great to see tons of tiny projects, sometimes you just need more pins, more FLASH, and more RAM. That's why we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
  4xAA Switchable Battery Pack w/Bare Wire: 4xAA Switchable Battery Pack with Bare Wire connection
